# Fritzing sketch schema_hodlCube_en (saved by Fritzing 0.9.6b)
perfboards: 1

parts:
  LED2 = LED - 5mm [color="Red (633nm)" current=20mA package="5 mm [THT]"]
  LED1 = LED - 5mm [color="Green (555nm)" current=20mA package="5 mm [THT]"]
  buz1 = Piezo Buzzer
  WeMos_D1_Mini = WeMos D1 Mini Lite
  R2 = Resistor [tolerance=±5% power=0.25W resistance=51 package=THT]
  R1 = Resistor [tolerance=±5% power=0.25W resistance=15 package=THT]
  1_3"_128x64_OLED = Module display OLED I2C 128x64 SSD1306 [package=THT]  # not connected
  SDA_SCK_GND_VDD = male pin header, 4 pins [form="♂ (male)"]

nets:
  N1: LED2.cathode, R2.Pin_1
  N2: LED2.anode, WeMos_D1_Mini.D6
  N3: LED1.cathode, R1.Pin_0
  N4: LED1.anode, WeMos_D1_Mini.D5
  N5: buz1.pin_1, R2.Pin_0, R1.Pin_1
  N6: buz1.pin_2, WeMos_D1_Mini.D7
  N7: WeMos_D1_Mini.3V3, SDA_SCK_GND_VDD.pin4
  N8: WeMos_D1_Mini.D1, SDA_SCK_GND_VDD.pin2
  N9: WeMos_D1_Mini.D2, SDA_SCK_GND_VDD.pin1

notes:
  black/brown
  purple/blue
  white/gray
  VDD(VCC) red wire w/ connector 7cm
  SDA yellow wire w/ connector 6cm
  SCK(SCL) purple/blue w/ connector 6cm
  GND black/brown w/ connector 6cm
  green LED green 4cm
  red LED orange 6cm
  buzzer white/gray 4cm
  negative black 4,5cm
  3V3 VDD(VCC)
  D7 buzzer
  D6 red LED
  D5 green LED
  D1 SCK(SCL)
  D2 SDA
  connectors rear view

custom parts:
  Piezo Buzzer: Part from https://www.nutsvolts.com/magazine/article/november2012_SmileysWorkshop modified to be .3 in spacing to match the adafruit buzzer 5V breadboard friendly part.
  WeMos D1 Mini Lite: A simple wifi board with 1MB flash based on ESP-8285
  Module display OLED I2C 128x64 SSD1306: Ecran OLED I2C SSD163 de 128x64 avec connexion I2C
